# Fritzing sketch your-turn (saved by Fritzing 1.0.0)

parts:
  60-row_breadboard = 60-row breadboard
  TTGO_T-Display = TTGO T-Display
  Yellow_pushbutton = Yellow pushbutton
  Yellow_LED = Yellow LED
  220_ohm_resistor = 220 ohm resistor
  Blue_potentiometer = Blue potentiometer
  Analog_joystick_(powered_from_3_3V) = Analog joystick (powered from 3.3V)

nets:
  GND: 60-row_breadboard.GL_button, 60-row_breadboard.GL_led, 60-row_breadboard.GL_board, 60-row_breadboard.GR_board, 60-row_breadboard.GR_joy, 60-row_breadboard.GR_pot, TTGO_T-Display.G, TTGO_T-Display.G2, TTGO_T-Display.G3, TTGO_T-Display.G4, TTGO_T-Display.G_R, Yellow_pushbutton.GND, Yellow_pushbutton.GND_R, Yellow_LED.Cathode, Blue_potentiometer.1, Analog_joystick_(powered_from_3_3V).GND
  N1: 60-row_breadboard.V_board, 60-row_breadboard.V_joy, 60-row_breadboard.V_pot, TTGO_T-Display.3V_L, TTGO_T-Display.3V, Blue_potentiometer.3, Analog_joystick_(powered_from_3_3V).+5V
  N2: TTGO_T-Display.2, Yellow_pushbutton.Signal, Yellow_pushbutton.Signal_R
  N3: TTGO_T-Display.15, 220_ohm_resistor.B
  N4: TTGO_T-Display.13, Blue_potentiometer.2
  N5: TTGO_T-Display.39, Analog_joystick_(powered_from_3_3V).VRx
  N6: TTGO_T-Display.32, Analog_joystick_(powered_from_3_3V).VRy
  N7: TTGO_T-Display.33, Analog_joystick_(powered_from_3_3V).SW
  N8: Yellow_LED.Anode, 220_ohm_resistor.A

custom parts:
  60-row breadboard: Your Turn documentation part, based on the course Lab 2 layout.
  TTGO T-Display: Your Turn documentation part, based on the course Lab 2 layout.
  Yellow pushbutton: Your Turn documentation part, based on the course Lab 2 layout.
  Yellow LED: Your Turn documentation part, based on the course Lab 2 layout.
  220 ohm resistor: Your Turn documentation part, based on the course Lab 2 layout.
  Blue potentiometer: Your Turn documentation part, based on the course Lab 2 layout.
  Analog joystick (powered from 3.3V): Your Turn documentation part, based on the course Lab 2 layout.
